# Fritzing sketch scheme (saved by Fritzing 0.9.3b)
breadboards: 1

parts:
  Součástka1 = Arduino Nano (Rev3.0)
  Nokia_5110_LCD_Module1 = Nokia 5110 LCD  # not connected
  MS1 = MS5611

nets:
  5V: Součástka1.5V, MS1.VIN

custom parts:
  Nokia 5110 LCD: Nokia 5110 Graphic 84*48 LCD module such as the Sparkfun LCD-10168 or the clones from Ebay. There is example code for the Arduino available from the Sparkfun site in https://learn.sparkfun.com/tutorials/graphic-lcd-hookup-guide This is a 3.3V device, if you are running it from a 5V micro you need a 5V tolorant level translator such as the 74ahc367 to protect the signal imputs. Rafa G. did a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
